// Logisim project test.circ as structural Verilog: 1 circuit, main circuit main
module main (
);

  wire and_1_out, and_2_out, and_3_out, and_4_out, clock_1_out, clock_2_out, clock_3_out, clock_4_out,
       clock_5_out, d_ff_1_q, decoder_1_out0, decoder_1_out1, decoder_1_out2, decoder_1_out3,
       demultiplexer_2_out8, j_k_ff_1_q, j_k_ff_2_q, not_1_out, not_2_out, not_3_out, not_4_out, not_5_out,
       not_6_out, or_1_out, t_ff_1_q, t_ff_2_qn, t_ff_3_q, t_ff_3_qn, t_ff_4_q;
  wire [1:0] or_2_out, register_10_q_2, subtractor_2_out;
  wire [3:0] register_10_q;
  wire [3:2] register_10_q_3;
  wire [7:0] rom_1_p1, rom_1_p2, rom_1_p3, rom_1_p4;
  wire [23:0] controlled_buffer_1_out, counter_1_q, PC, register_9_q;
  wire [25:0] shifter_1_out;
  wire [31:0] adder_1_out, controlled_buffer_3_out, demultiplexer_1_out0, demultiplexer_1_out1,
       divider_1_out, multiplexer_2_out, multiplier_2_out, register_5_q, register_6_q, register_7_q,
       register_8_q, subtractor_1_out;
  wire [31:24] register_9_q_2;

  T_Flip_Flop t_ff_1 (.T(clock_1_out), .clk(clock_1_out), .Q(t_ff_1_q));  // open: Qn, reset, preset
  Clock clock_1 (.out(clock_1_out));
  Counter #(.max('hffffff), .width(24)) counter_1 (
    .load(demultiplexer_2_out8), .clk(t_ff_1_q), .D(register_9_q), .Q(counter_1_q));  // open: clr, up, count, carry
  Decoder #(.select(2)) decoder_1 (
    .out0(decoder_1_out0), .out1(decoder_1_out1), .out2(decoder_1_out2), .out3(decoder_1_out3));  // open: sel, en
  Register register_1 (.en(decoder_1_out0));  // open: D, clk, Q, clr
  Register register_2 (.en(decoder_1_out1));  // open: D, clk, Q, clr
  Register register_3 (.en(decoder_1_out2));  // open: D, clk, Q, clr
  Register register_4 (.en(decoder_1_out3));  // open: D, clk, Q, clr
  // ROM #(.addrWidth(24), .line("quad")) rom_1: pin names not known; wires that end beside it: rom_1_p1, rom_1_p2, rom_1_p3, rom_1_p4
  Multiplexer #(.width(24)) multiplexer_1 (.in0(PC), .sel(1'b0));  // open: in1, out
  Multiplier #(.width(24)) multiplier_1 (.a(counter_1_q), .b(24'h4), .out(PC));  // open: cin, cout
  Clock clock_2 (.out(clock_2_out));
  T_Flip_Flop t_ff_2 (.T(clock_2_out), .clk(clock_2_out), .Qn(t_ff_2_qn));  // open: Q, reset, preset
  Register #(.width(32)) register_5 (
    .D({rom_1_p4, rom_1_p3, rom_1_p2, rom_1_p1}), .en(t_ff_2_qn), .clk(clock_2_out), .Q(register_5_q),
    .clr(demultiplexer_2_out8));
  J_K_Flip_Flop j_k_ff_1 (
    .J(t_ff_2_qn), .K(clock_2_out), .clk(clock_2_out), .Q(j_k_ff_1_q));  // open: Qn, preset, reset
  Register #(.width(32)) register_6 (
    .D(register_5_q), .en(j_k_ff_1_q), .clk(j_k_ff_1_q), .Q(register_6_q));  // open: clr
  // Probe on demultiplexer_1_out0
  // Probe on register_6_q[20:0]
  Register #(.width(32)) register_7 (
    .D(demultiplexer_1_out0), .en(and_1_out), .clk(clock_4_out), .Q(register_7_q));  // open: clr
  Register #(.width(32)) register_8 (
    .D(demultiplexer_1_out1), .en(and_3_out), .clk(clock_4_out), .Q(register_8_q));  // open: clr
  Demultiplexer #(.width(32)) demultiplexer_1 (
    .out0(demultiplexer_1_out0), .out1(demultiplexer_1_out1), .in({{8{1'b0}}, controlled_buffer_1_out}),
    .sel(and_3_out));
  // Probe on {{8{1'b0}}, controlled_buffer_1_out}
  // Probe on register_6_q[25:0]
  not not_1 (not_1_out, register_6_q[24]);
  not not_2 (not_2_out, register_6_q[25]);
  not not_3 (not_3_out, register_6_q[27]);
  not not_4 (not_4_out, register_6_q[29]);
  not not_5 (not_5_out, register_6_q[30]);
  not not_6 (not_6_out, register_6_q[31]);
  Shifter #(.width(26)) shifter_1 (.in(register_6_q[25:0]), .\dist (5'b00010), .out(shifter_1_out));
  and and_1 (and_1_out, and_2_out, t_ff_3_qn);
  T_Flip_Flop t_ff_3 (.T(and_2_out), .clk(clock_3_out), .Q(t_ff_3_q), .Qn(t_ff_3_qn));  // open: reset, preset
  and and_2 (and_2_out, not_1_out, not_2_out, register_6_q[26], not_3_out, register_6_q[28], not_4_out, not_5_out, not_6_out);
  Clock clock_3 (.out(clock_3_out));
  Clock clock_4 (.out(clock_4_out));
  assign controlled_buffer_1_out = and_1_out ? shifter_1_out[23:0] : 24'bz;  // Controlled_Buffer controlled_buffer_1
  // Probe on register_7_q
  Adder #(.width(32)) adder_1 (.a(register_7_q), .b(register_8_q), .out(adder_1_out));  // open: cin, cout
  Subtractor #(.width(32)) subtractor_1 (
    .a(register_7_q), .b(register_8_q), .out(subtractor_1_out));  // open: bin, bout
  Multiplier #(.width(32)) multiplier_2 (
    .a(register_7_q), .b(register_8_q), .out(multiplier_2_out));  // open: cin, cout
  Divider #(.width(32)) divider_1 (.a(register_7_q), .b(register_8_q), .out(divider_1_out));  // open: upper, rem
  assign controlled_buffer_1_out = and_3_out ? PC : 24'bz;  // Controlled_Buffer controlled_buffer_2
  and and_3 (and_3_out, and_2_out, t_ff_3_q);
  Multiplexer #(.select(2), .width(32)) multiplexer_2 (
    .in0(adder_1_out), .in1(subtractor_1_out), .in2(multiplier_2_out), .in3(divider_1_out),
    .out(multiplexer_2_out), .sel(subtractor_2_out));
  Subtractor #(.width(2)) subtractor_2 (.a(or_2_out), .b(2'b01), .out(subtractor_2_out));  // open: bin, bout
  J_K_Flip_Flop j_k_ff_2 (.J(t_ff_3_q), .K(clock_3_out), .clk(clock_3_out), .Q(j_k_ff_2_q));  // open: Qn, preset, reset
  Register #(.width(32)) register_9 (
    .D(controlled_buffer_3_out), .en(or_1_out), .clk(clock_4_out), .Q({register_9_q_2, register_9_q}));  // open: clr
  // Probe on controlled_buffer_3_out
  assign controlled_buffer_3_out = or_1_out ? multiplexer_2_out : 32'bz;  // Controlled_Buffer controlled_buffer_3
  or or_1 (or_1_out, or_2_out[1], or_2_out[0]);
  assign or_2_out = register_10_q_2;  // OR_Gate or_2, 2 bits wide OR_Gate
  Register register_10 (
    .D(8'h18), .en(j_k_ff_2_q), .clk(j_k_ff_2_q), .Q({register_10_q_3, register_10_q_2, register_10_q}),
    .clr(d_ff_1_q));
  T_Flip_Flop t_ff_4 (.T(j_k_ff_2_q), .clk(clock_5_out), .Q(t_ff_4_q), .reset(d_ff_1_q));  // open: Qn, preset
  Clock clock_5 (.out(clock_5_out));
  D_Flip_Flop d_ff_1 (.D(t_ff_4_q), .clk(clock_5_out), .Q(d_ff_1_q));  // open: Qn, preset, reset
  and and_4 (and_4_out, 1'b1, t_ff_4_q);
  Demultiplexer #(.select(4)) demultiplexer_2 (
    .out8(demultiplexer_2_out8), .in(and_4_out), .sel(register_10_q));  // open: out0, out1, out2, out3, out4, out5, out6, out7, out9, out10, out11, out12, out13, out14, out15

  // Notes on the sheet:
  //   contents of rom_1 (hex, n*v repeats v):
  //   fe ff ff 14 4*0 44 55 66 88
endmodule
